# Fritzing sketch PiPower HAT (saved by Fritzing 0.9.3b)
circuit board: 6.52541cm x 5.62539cm
breadboards: 1

parts:
  RPi = Cobbler Plus Cable
  SW1 = male pin header, 4 pins [form="♂ (male)"]
  Arduino = Arduino Pro Mini (5V)
  Q1 = Basic FET P-Channel [package="TO220 [THT]"]
  R1 = Resistor [tolerance=±5% resistance=10k package=THT]
  J1 = USB Connectors [package="Standard Shell SMT"]

nets:
  N1: RPi.5.0V#1, Q1.drain
  N2: RPi.TXD, Arduino.RXI
  GND: RPi.GND#8, RPi.GND#24, RPi.GND#38, SW1.pin2, SW1.pin3, Arduino.GND, J1.GND
  N3: RPi.RXD, Arduino.TXO
  N4: SW1.pin1, Arduino.SCK
  N5: SW1.pin4, Arduino.D3
  N6: Arduino.RAW, Q1.source, R1.Pin_1, J1.VCC
  N7: Arduino.D10, Q1.gate, R1.Pin_0

notes:
  + -  - +
  PiPower HAT v1
  k5map@arrl.net

custom parts:
  Cobbler Plus Cable: The Cobbler Plus is an add on prototyping board from Adafruit specifically designed for the Raspberry Pi B+ that can break out all those tasty power, GPIO, I2C and SPI pins from the 40-pin header onto a solderless breadboard. This set will make "cobbling together" prototypes with the Pi super easy. The Cobbler Plus can plug into any solderless breadboard.
  USB Connectors: Hirose-USB-Micro-B_SMD - Stanard (Bottom mount), Shell SMT
